# Fritzing sketch fade circuit (saved by Fritzing 0.9.3b)
breadboards: 1

parts:
  Part1 = Arduino Uno (Rev3)
  R1 = Resistor [tolerance=±5% resistance=220 package="1206 [SMD]"]
  R2 = Resistor [tolerance=±5% resistance=220 package="1206 [SMD]"]
  LED1 = smd LED [color="Red (633nm)" package="1206 [SMD]"]
  LED2 = smd LED [color="Red (633nm)" package="1206 [SMD]"]

nets:
  N1: Part1.D9_PWM, R1.Pin_0, R2.Pin_0
  N2: Part1.GND, LED1.cathode, LED2.cathode
  N3: R1.Pin_1, LED2.anode
  N4: R2.Pin_1, LED1.anode
